# Fritzing sketch Lego car with IR sensors (saved by Fritzing 0.9.3b)
breadboards: 1

parts:
  Onderdeel1 = Arduino Nano (Rev3.0)
  J1 = Infrared Proximity Sensor
  J2 = Infrared Proximity Sensor
  M1 = DC Motor
  M2 = DC Motor
  Onderdeel2 = HC-SR04 Ultrasonic Rangemeter
  Onderdeel3 = HC-SR04 Ultrasonic Rangemeter
  S1 = H-Bridge with L298N
  VCC1 = Battery block 9V

nets:
  GND: Onderdeel1.GND, J1.GND, J2.GND, Onderdeel2.GND, Onderdeel3.GND, S1.GND, S1.ENB, VCC1.-
  N1: Onderdeel1.D5, S1.IN1
  N2: Onderdeel1.D6, S1.IN2
  N3: Onderdeel1.D11/MOSI, S1.IN4
  N4: Onderdeel1.D12/MISO, S1.IN3
  VIN: Onderdeel1.VIN, S1.12V, VCC1.+
  VCC: Onderdeel1.5V, J1.Vcc, J2.Vcc, Onderdeel2.VCC, Onderdeel3.VCC, S1.ENB-5V
  N5: Onderdeel1.A5, Onderdeel3.Echo
  N6: Onderdeel1.A4, J1.Vout
  N7: Onderdeel1.A3, J2.Vout
  N8: Onderdeel1.A2, Onderdeel2.Echo
  N9: M1.pin_1, S1.M1-02
  N10: M1.pin_2, S1.M1-01
  N11: M2.pin_1, S1.M2-01, S1.M2-02

custom parts:
  H-Bridge with L298N: h-bridge
